// Logisim project arq-de-comp.circ as structural Verilog: 22 circuits, main circuit latch_sr
module latch_sr (
  input  S,
  input  R,
  output Q_prime,
  output Q
);

  nor nor_1 (Q_prime, S, Q);
  nor nor_2 (Q, Q_prime, R);
endmodule

module latch_sr_barrado (
  input  S,
  input  R,
  output Q_prime,
  output Q
);

  nor nor_1 (Q_prime, ~S, Q);  // NOR_Gate
  nor nor_2 (Q, Q_prime, ~R);  // NOR_Gate
endmodule

module latch_sr_controlado (
  input  S,
  input  C,
  input  R,
  output Q_prime,
  output Q
);

  wire and_1_out, and_2_out;

  and and_1 (and_1_out, S, C);
  and and_2 (and_2_out, C, R);
  nor nor_1 (Q_prime, and_1_out, Q);
  nor nor_2 (Q, Q_prime, and_2_out);
endmodule

module latch_d (
  input  D,
  input  C,
  output Q_prime,
  output Q
);

  wire not_1_out;

  not not_1 (not_1_out, D);
  latch_sr_controlado latch_sr_controlado_1 (.S(D), .C(C), .R(not_1_out), .Q_prime(Q_prime), .Q(Q));
endmodule

module ff_d (
  input  D,
  output Q_prime,
  output Q
);

  wire CLK_out, latch_d_2_q, not_1_out;

  Clock CLK (.out(CLK_out));
  latch_d latch_d_1 (.D(latch_d_2_q), .C(not_1_out), .Q_prime(Q_prime), .Q(Q));
  latch_d latch_d_2 (.D(D), .C(CLK_out), .Q(latch_d_2_q));  // open: Q_prime
  not not_1 (not_1_out, CLK_out);

  // Notes on the sheet:
  //   Y
endmodule

module ff_jk (
  input  J,
  input  K,
  output Q,
  output Q_prime
);

  wire and_1_out, and_2_out, clock_1_out, or_1_out;

  and and_1 (and_1_out, Q_prime, J);
  and and_2 (and_2_out, ~K, Q);  // AND_Gate
  Clock clock_1 (.out(clock_1_out));
  or or_1 (or_1_out, and_1_out, and_2_out);
  D_Flip_Flop #(.trigger("high")) d_ff_1 (
    .clk(clock_1_out), .D(or_1_out), .Q(Q), .Qn(Q_prime));  // open: preset, en, reset
endmodule

module ff_t (
  input  T,
  output out_2,
  output out_3
);

  wire clock_1_out, j_k_ff_1_qn;

  Clock clock_1 (.out(clock_1_out));
  J_K_Flip_Flop j_k_ff_1 (.J(T), .clk(clock_1_out), .K(T), .Q(out_2), .Qn(j_k_ff_1_qn));  // open: preset, en, reset
  not not_1 (out_3, j_k_ff_1_qn);
endmodule

module cc_ff (
  input  X,
  output A,
  output A_prime,
  output B,
  output B_prime,
  output Y
);

  wire and_1_out, and_2_out, and_3_out, clock_1_out, or_2_out;

  and and_1 (and_1_out, A, X);
  and and_2 (and_2_out, X, B);
  and and_3 (and_3_out, A_prime, X);
  or or_1 (Y, B, A);
  or or_2 (or_2_out, and_1_out, and_2_out);
  D_Flip_Flop d_ff_1 (.clk(clock_1_out), .D(or_2_out), .Q(A), .Qn(A_prime));  // open: preset, en, reset
  Clock clock_1 (.out(clock_1_out));
  D_Flip_Flop d_ff_2 (.clk(clock_1_out), .D(and_3_out), .Q(B), .Qn(B_prime));  // open: preset, en, reset
endmodule

module ULA___mult_8x1 (
  input  [7:0] A,
  input  [7:0] B,
  input  [2:0] S,
  output [7:0] X
);

  wire [7:0] adder_1_out, adder_2_out, adder_3_out, and_1_out, not_1_out, or_1_out, xor_1_out;

  assign not_1_out = ~A;  // NOT_Gate not_1, 8 bits wide
  Adder adder_1 (.a(A), .b(B), .out(adder_1_out));  // open: cin, cout
  Adder adder_2 (.a(A), .b(B), .out(adder_2_out));  // open: cin, cout
  assign and_1_out = A & B;  // AND_Gate and_1, 8 bits wide
  assign or_1_out = A | B;  // OR_Gate or_1, 8 bits wide
  assign xor_1_out = A ^ B;  // XOR_Gate xor_1, 8 bits wide
  Adder adder_3 (.a(A), .b({8{1'b1}}), .out(adder_3_out));  // open: cin, cout
  Multiplexer #(.select(3), .width(8)) multiplexer_1 (
    .in0(adder_1_out), .in1(adder_2_out), .in2(adder_3_out), .in3(A), .in4(and_1_out), .in5(or_1_out),
    .in6(xor_1_out), .in7(not_1_out), .out(X), .sel(S));  // open: en
endmodule

module mult_2x1 (
  input  A,
  input  B,
  input  S,
  output X
);

  wire and_1_out, and_2_out;

  and and_1 (and_1_out, A, ~S);  // AND_Gate
  and and_2 (and_2_out, B, S);
  or or_1 (X, and_1_out, and_2_out);
endmodule

module mult_4x1 (
  input  A,
  input  B,
  input  C,
  input  D,
  input  S0,
  input  S1,
  output x
);

  wire and_1_out, and_2_out, and_3_out, and_4_out, and_5_out, and_6_out, and_7_out, and_8_out;

  and and_1 (and_1_out, ~S0, ~S1);  // AND_Gate
  and and_2 (and_2_out, ~S0, S1);  // AND_Gate
  and and_3 (and_3_out, S0, ~S1);  // AND_Gate
  and and_4 (and_4_out, S0, S1);
  and and_5 (and_5_out, A, and_1_out);
  and and_6 (and_6_out, B, and_2_out);
  and and_7 (and_7_out, C, and_3_out);
  and and_8 (and_8_out, D, and_4_out);
  or or_1 (x, and_5_out, and_6_out, and_7_out, and_8_out);
endmodule

module mult_8x1 (
  input  S2,
  input  S1,
  input  S0,
  input  L0,
  input  L1,
  input  L2,
  input  L3,
  input  L4,
  input  L5,
  input  L6,
  input  L7,
  output X
);

  wire and_1_out, and_2_out, and_3_out, and_4_out, and_5_out, and_6_out, and_7_out, and_8_out, and_9_out,
       and_10_out, and_11_out, and_12_out, and_13_out, and_14_out, and_15_out, and_16_out;

  and and_1 (and_1_out, S0, S1, S2);
  and and_2 (and_2_out, S0, S1, S2);
  and and_3 (and_3_out, and_1_out, L0);
  and and_4 (and_4_out, and_2_out, L1);
  and and_5 (and_5_out, S0, S1, S2);
  and and_6 (and_6_out, S0, S1, S2);
  and and_7 (and_7_out, S0, S1, S2);
  and and_8 (and_8_out, and_7_out, L4);
  and and_9 (and_9_out, and_6_out, L3);
  and and_10 (and_10_out, and_5_out, L2);
  or or_1 (X, and_3_out, and_4_out, and_10_out, and_9_out, and_8_out, and_14_out, and_15_out, and_16_out);
  and and_11 (and_11_out, S0, S1, S2);
  and and_12 (and_12_out, S0, S1, S2);
  and and_13 (and_13_out, S0, S1, S2);
  and and_14 (and_14_out, and_11_out, L5);
  and and_15 (and_15_out, and_12_out, L6);
  and and_16 (and_16_out, and_13_out, L7);
endmodule

module mult_paralelo (
  input  E0,
  input  E1,
  input  E2,
  input  E3,
  input  [1:0] A,
  output X,
  output X_2
);

  Multiplexer #(.select(2), .enable("false")) multiplexer_1 (.in0(E0), .in1(E1), .in2(E2), .in3(E3), .out(X), .sel(A));
  Multiplexer #(.select(2), .enable("false")) multiplexer_2 (
    .in0(E0), .in1(E1), .in2(E1), .in3(E1), .out(X_2), .sel(A));
endmodule

module mult_serie (
  input  in_1,
  input  in_2,
  input  in_3,
  input  in_4,
  input  in_5,
  input  in_6,
  input  in_7,
  input  in_8,
  input  in_9,
  input  in_10,
  input  in_11,
  input  [1:0] in_12,
  input  in_13,
  input  in_14,
  input  in_15,
  input  in_16,
  input  in_17,
  input  [1:0] in_18,
  output out_19
);

  wire multiplexer_1_out, multiplexer_2_out, multiplexer_3_out, multiplexer_4_out;

  Multiplexer #(.select(2), .enable("false")) multiplexer_1 (
    .in0(in_1), .in1(in_2), .in2(in_3), .in3(in_4), .out(multiplexer_1_out), .sel(in_18));
  Multiplexer #(.select(2), .enable("false")) multiplexer_2 (
    .in0(in_5), .in1(in_6), .in2(in_7), .in3(in_8), .out(multiplexer_2_out), .sel(in_18));
  Multiplexer #(.select(2), .enable("false")) multiplexer_3 (
    .in0(in_9), .in1(in_10), .in2(in_11), .in3(in_13), .out(multiplexer_3_out), .sel(in_18));
  Multiplexer #(.select(2), .enable("false")) multiplexer_4 (
    .in0(in_14), .in1(in_15), .in2(in_16), .in3(in_17), .out(multiplexer_4_out), .sel(in_18));
  Multiplexer #(.select(2), .enable("false")) multiplexer_5 (
    .in0(multiplexer_1_out), .in1(multiplexer_2_out), .in2(multiplexer_3_out), .in3(multiplexer_4_out),
    .out(out_19), .sel(in_12));
endmodule

module half_adder (
  input  A,
  input  B,
  output Soma,
  output Cout
);

  xor xor_1 (Soma, A, B);
  and and_1 (Cout, A, B);
endmodule

module full_adder (
  input  cin,
  input  a,
  input  b,
  output soma,
  output cout
);

  wire half_adder_1_cout, half_adder_1_soma, half_adder_2_cout;

  half_adder half_adder_1 (.A(a), .B(b), .Soma(half_adder_1_soma), .Cout(half_adder_1_cout));
  half_adder half_adder_2 (.A(cin), .B(half_adder_1_soma), .Soma(soma), .Cout(half_adder_2_cout));
  or or_1 (cout, half_adder_2_cout, half_adder_1_cout);
endmodule

module somador___4b (
  input  msb,
  input  in_2,
  input  in_3,
  input  in_4,
  input  in_5,
  input  in_6,
  input  in_7,
  input  lsb,
  output lsb_2,
  output out_10,
  output out_11,
  output msb_2,
  output Overflow
);

  wire full_adder_1_cout, full_adder_2_cout, half_adder_1_cout;

  half_adder half_adder_1 (.A(lsb), .B(in_4), .Soma(lsb_2), .Cout(half_adder_1_cout));
  full_adder full_adder_1 (.cin(half_adder_1_cout), .a(in_7), .b(in_3), .soma(out_10), .cout(full_adder_1_cout));
  full_adder full_adder_2 (.cin(full_adder_1_cout), .a(in_6), .b(in_2), .soma(out_11), .cout(full_adder_2_cout));
  full_adder full_adder_3 (.cin(full_adder_2_cout), .a(in_5), .b(msb), .soma(msb_2), .cout(Overflow));
endmodule

module deco (
  input  B1,
  input  B0,
  output E0,
  output E1,
  output E2,
  output E3
);

  and and_1 (E0, ~B1, ~B0);  // AND_Gate
  and and_2 (E1, ~B1, B0);  // AND_Gate
  and and_3 (E2, B1, ~B0);  // AND_Gate
  and and_4 (E3, B1, B0);
endmodule

module deco_2x4 (
  input  B1,
  input  B0,
  output out_3,
  output out_4,
  output out_5,
  output out_6
);

  deco deco_1 (.B1(B1), .B0(B0), .E0(out_3), .E1(out_4), .E2(out_5), .E3(out_6));
endmodule

module deco_3x8 (
  input  Enable,
  input  [2:0] Bits,
  output E0,
  output E1,
  output E2,
  output E3,
  output E4,
  output E5,
  output E6,
  output out_10
);

  Decoder #(.select(3)) decoder_1 (
    .out0(E0), .out1(E1), .out2(E2), .out3(E3), .out4(E4), .out5(E5), .out6(E6), .out7(out_10), .sel(Bits),
    .en(Enable));
endmodule

module deco_3x8_duplo (
  input  Enable,
  input  [2:0] Bits,
  output E0,
  output E1,
  output E2,
  output E3,
  output E4,
  output E5,
  output E6,
  output E8,
  output out_11,
  output E9,
  output E10,
  output E11,
  output E12,
  output E13,
  output E14,
  output E15
);

  wire clock_1_out, not_1_out;

  Clock clock_1 (.out(clock_1_out));
  Decoder #(.select(3)) decoder_1 (
    .out0(E0), .out1(E1), .out2(E2), .out3(E3), .out4(E4), .out5(E5), .out6(E6), .out7(out_11), .sel(Bits),
    .en(not_1_out));
  not not_1 (not_1_out, clock_1_out);
  Decoder #(.select(3)) decoder_2 (
    .out0(E8), .out1(E9), .out2(E10), .out3(E11), .out4(E12), .out5(E13), .out6(E14), .out7(E15), .sel(Bits),
    .en(clock_1_out));
endmodule

module deco_min_termer (
  input  in_1,
  input  [2:0] in_2,
  output out_3,
  output out_4
);

  wire deco_3x8_1_e0, deco_3x8_1_e1, deco_3x8_1_e5, deco_3x8_1_out_10;

  deco_3x8 deco_3x8_1 (
    .Enable(in_1), .Bits(in_2), .E0(deco_3x8_1_e0), .E1(deco_3x8_1_e1), .E2(out_3), .E5(deco_3x8_1_e5),
    .out_10(deco_3x8_1_out_10));  // open: E3, E4, E6
  or or_1 (out_4, deco_3x8_1_e0, deco_3x8_1_e1, deco_3x8_1_e5, deco_3x8_1_out_10);
endmodule
